# Fritzing sketch pcb for micro v2 with new plug in buttons (saved by Fritzing 0.9.3b)
circuit board: 3.72135cm x 4.99346cm
breadboards: 1

parts:
  Pro_Micro1 = Arduino Pro Mini v13
  screen_1 = female pin header, 7 pins [form="♀ (female)"]
  rotary_encoder = female pin header, 5 pins [form="♀ (female)"]
  buttons_1-_5 = female pin header, 8 pins [form="♀ (female)"]
  Button5 = female pin header, 5 pins [form="♀ (female)"]
  p/g = female pin header, 2 pins [form="♀ (female)"]

nets:
  N1: Pro_Micro1.VCC, screen_1.pin1, rotary_encoder.pin1, buttons_1-_5.pin7, Button5.pin1, p/g.pin1
  N2: Pro_Micro1.GND, screen_1.pin2, rotary_encoder.pin2, buttons_1-_5.pin6, Button5.pin4, p/g.pin2
  N3: Pro_Micro1.A2, buttons_1-_5.pin2
  N4: Pro_Micro1.A1, buttons_1-_5.pin3
  N5: Pro_Micro1.A0, buttons_1-_5.pin4
  N6: Pro_Micro1.D13/SCK, screen_1.pin3
  N7: Pro_Micro1.D11_PWM/MOSI, screen_1.pin4
  N8: Pro_Micro1.D10_PWM/SS, Pro_Micro1.D8, screen_1.pin5, screen_1.pin6
  N9: Pro_Micro1.D9_PWM, screen_1.pin7
  N10: Pro_Micro1.D7, buttons_1-_5.pin5
  N11: Pro_Micro1.D6_PWM, buttons_1-_5.pin1
  N12: Pro_Micro1.D5_PWM, rotary_encoder.pin5
  N13: Pro_Micro1.D4, rotary_encoder.pin4
  N14: Pro_Micro1.D3_PWM, rotary_encoder.pin3
  N15: Pro_Micro1.D2, Button5.pin3
  N16: buttons_1-_5.pin8, Button5.pin2
