# Fritzing sketch pcb for push buttons 2 (saved by Fritzing 0.9.3b)
circuit board: 7.72428cm x 2.51915cm
breadboards: 1

parts:
  Btn = Pushbutton [package="[THT]"]
  Neo = ws2812b [package="smd 2812b"]
  Btn1 = Pushbutton [package="[THT]"]
  Neo1 = ws2812b [package="smd 2812b"]
  Btn2 = Pushbutton [package="[THT]"]
  Neo2 = ws2812b [package="smd 2812b"]
  Btn3 = Pushbutton [package="[THT]"]
  Neo3 = ws2812b [package="smd 2812b"]
  10k1 = Resistor [tolerance=±5% resistance=10k package=THT]
  10k4 = Resistor [tolerance=±5% resistance=10k package=THT]
  10k5 = Resistor [tolerance=±5% resistance=10k package=THT]
  10k6 = Resistor [tolerance=±5% resistance=10k package=THT]
  header = female pin header, 8 pins [form="♀ (female)"]

nets:
  N1: Btn.Pin_1, Btn.Pin_2, 10k4.Pin_1, header.pin2
  N2: Btn.Pin_3, Btn.Pin_4, Btn1.Pin_3, Btn1.Pin_4, Btn2.Pin_3, Btn2.Pin_4, Btn3.Pin_3, Btn3.Pin_4, header.pin7
  VDD: Neo.VDD, Neo1.VDD, Neo2.VDD, Neo3.VDD
  N3: Neo.DOUT, Neo1.DIN
  VSS: Neo.VSS, Neo1.VSS, Neo2.VSS, Neo3.VSS, 10k1.Pin_0, 10k4.Pin_0, 10k5.Pin_0, 10k6.Pin_0, header.pin6
  N4: Neo.DIN, header.pin1
  N5: Btn1.Pin_1, Btn1.Pin_2, 10k1.Pin_1, header.pin3
  N6: Neo1.DOUT, Neo2.DIN
  N7: Btn2.Pin_1, Btn2.Pin_2, 10k5.Pin_1, header.pin4
  N8: Neo2.DOUT, Neo3.DIN
  N9: Btn3.Pin_1, Btn3.Pin_2, 10k6.Pin_1, header.pin5
  N10: Neo3.DOUT, header.pin8
