# Fritzing sketch pcb for push buttons (saved by Fritzing 0.9.3b)
circuit board: 2.24428cm x 1.76839cm
breadboards: 1

parts:
  Neo = ws2812b [package="smd 2812b"]
  Btn = Pushbutton [package="[THT]"]
  J3 = female pin header, 5 pins [form="♀ (female)"]
  10k = Resistor [tolerance=±5% resistance=10k package=THT]

nets:
  N1: Neo.VDD, Btn.Pin_3, Btn.Pin_4, J3.pin1
  N2: Neo.DOUT, J3.pin5
  N3: Neo.VSS, J3.pin4, 10k.Pin_1
  N4: Neo.DIN, J3.pin2
  N5: Btn.Pin_1, Btn.Pin_2, J3.pin3, 10k.Pin_0
