# Fritzing sketch pcb for rotary encoder (saved by Fritzing 0.9.3b)
circuit board: 2.23991cm x 2.21164cm
breadboards: 1

parts:
  Rotary_Encoder = Rotary Encoder with Knob
  fhp = female pin header, 5 pins [form="♀ (female)"]
  10k = Resistor [tolerance=±5% resistance=10k package=THT]
  10k1 = Resistor [tolerance=±5% resistance=10k package=THT]
  10k2 = Resistor [tolerance=±5% resistance=10k package=THT]

nets:
  N1: Rotary_Encoder.no_name_yet#1, fhp.pin2, 10k.Pin_0
  N2: Rotary_Encoder.no_name_yet#2, fhp.pin4, 10k2.Pin_0
  N3: Rotary_Encoder.no_name_yet#3, fhp.pin1, 10k1.Pin_0
  N4: Rotary_Encoder.no_name_yet#4, fhp.pin3
  N5: Rotary_Encoder.no_name_yet#5, 10k2.Pin_1
  N6: fhp.pin5, 10k.Pin_1, 10k1.Pin_1

custom parts:
  Rotary Encoder with Knob: Rotary Encoder with 1/4" Shaft and Knob
